# Fritzing sketch breadboard_diagram (saved by Fritzing 0.7.4b)
breadboards: 1

parts:
  Part1 = Breakout Board for Electret Microphone
  U1 = Arduino Mega
  C1 = Electrolytic Capacitor [capacitance=1µF package="100 mil [THT, electrolytic]"]
  C2 = Electrolytic Capacitor [capacitance=1µF package="100 mil [THT, electrolytic]"]
  R1 = Resistor [tolerance=±5% resistance=150 package=THT]
  R2 = Resistor [tolerance=±5% resistance=150 package=THT]
  LED1 = LED - 5mm [color="White (4500K)" package="5 mm [THT]"]
  LED2 = LED - 5mm [color="White (4500K)" package="5 mm [THT]"]
  TRS1 = Stereo Jack (TRS) 3.5mm [package="PG203J [THT]"]

nets:
  GND: Part1.GND, U1.GND, R1.Pin_1, R2.Pin_1, TRS1.Sleeve
  N1: Part1.AUD, C1.-
  N2: U1.D10, C2.+
  N3: U1.D9, LED1.anode, LED2.anode
  N4: U1.A1, C1.+
  N5: R1.Pin_0, LED2.cathode
  N6: R2.Pin_0, LED1.cathode
